# Fritzing sketch shcematics_countdown_7seg_w_adustable_time (saved by Fritzing 0.9.0b)
breadboards: 1

parts:
  Part1 = Arduino Uno (Rev3)
  U1 = 7-SEGMENT-4DIGIT [package=7-segment-4digit-youngsun]
  R1 = Resistor [tolerance=±5% resistance=220 package=THT]
  R2 = Resistor [tolerance=±5% resistance=220 package=THT]
  R3 = Resistor [tolerance=±5% resistance=220 package=THT]
  R4 = Resistor [tolerance=±5% resistance=220 package=THT]
  S1 = Pushbutton [package="[THT]"]
  U2 = POT [package=pot_mammoth]
  J1 = Piezo Speaker
  R5 = Resistor [tolerance=±5% resistance=10k package="0603 [SMD]"]
  R6 = Resistor [tolerance=±5% resistance=100 package="0603 [SMD]"]

nets:
  N1: Part1.A0, U2.S
  N2: Part1.D8, U1.3
  N3: Part1.D9_PWM, R1.Pin_0
  N4: Part1.D10_PWM/SS, R2.Pin_0
  N5: Part1.D11_PWM/MOSI, R3.Pin_0
  N6: Part1.D12/MISO, R4.Pin_0
  N7: Part1.D13/SCK, R5.Pin_0
  N8: Part1.GND, U2.A, J1.pin2
  N9: Part1.D0/RX, R6.Pin_1
  N10: Part1.D1/TX, U1.13
  N11: Part1.D2, U1.7
  N12: Part1.D3_PWM, U1.4
  N13: Part1.D4, U1.2
  N14: Part1.D5_PWM, U1.1
  N15: Part1.D6_PWM, U1.11
  N16: Part1.D7, U1.5
  N17: Part1.5V, S1.Pin_2, U2.E
  N18: U1.6, R4.Pin_1
  N19: U1.8, R3.Pin_1
  N20: U1.9, R2.Pin_1
  N21: U1.14, R1.Pin_1
  N22: S1.Pin_3, R5.Pin_1
  N23: J1.pin1, R6.Pin_0
